# Fritzing sketch colorchanger (saved by Fritzing 0.7.1b)
breadboards: 1

parts:
  Teensy1 = Teensy 2.0
  S1 = Pushbutton [package="[THT]"]
  LED1 = RGB LED (com. anode, rbg) [package="5 mm [THT]"]
  R1 = Resistor [tolerance=±5% resistance=220 package=THT]
  R2 = Resistor [tolerance=±5% resistance=220 package=THT]
  R3 = Resistor [tolerance=±5% resistance=220 package=THT]

nets:
  N1: Teensy1.GND, S1.Pin_3, S1.Pin_4, LED1.common_anode
  N2: Teensy1.D7, R3.Pin_1
  N3: Teensy1.B4, S1.Pin_1, S1.Pin_2
  N4: Teensy1.B5, R2.Pin_1
  N5: Teensy1.B6, R1.Pin_1
  N6: LED1.red_cathode, R1.Pin_0
  N7: LED1.blue_cathode, R2.Pin_0
  N8: LED1.green_cathode, R3.Pin_0
